# Fritzing sketch ESP8266-Relay-Control-v1.0 (saved by Fritzing 0.9.3b)
circuit board: 7.54471cm x 6.28221cm
breadboards: 1

parts:
  U1 = NodeMCU V1.0
  R1 = Resistor [tolerance=±5% resistance=220 package=THT]
  R2 = Resistor [tolerance=±5% resistance=220 package=THT]
  R3 = Resistor [tolerance=±5% resistance=220 package=THT]
  R4 = Resistor [tolerance=±5% resistance=220 package=THT]
  LED3 = LED - 5mm [color="Green (570nm)" package="5 mm [THT]"]
  LED4 = LED - 5mm [color="Blue (470nm)" package="5 mm [THT]"]
  LED2 = LED - 5mm [color="Yellow (595nm)" package="5 mm [THT]"]
  LED1 = LED - 5mm [color="Red (633nm)" package="5 mm [THT]"]
  Pad1 = Pad [width=71.825555555555553 height=59.407777777777781 connect=center]  # not connected

nets:
  N1: U1.GND, LED3.cathode, LED4.cathode, LED2.cathode, LED1.cathode
  N2: U1.D5, R1.Pin_0
  N3: U1.D6, R2.Pin_0
  N4: U1.D7, R3.Pin_0
  N5: U1.D8, R4.Pin_0
  N6: R1.Pin_1, LED1.anode
  N7: R2.Pin_1, LED2.anode
  N8: R3.Pin_1, LED3.anode
  N9: R4.Pin_1, LED4.anode

custom parts:
  NodeMCU V1.0: ESP8266 based NodeMCU
